# Fritzing sketch WRO-2024-Future-Engineers (saved by Fritzing 0.9.10b)
# 18650 Li-ion Battery: CC-BY Dr Kristofer Chan, King's College London/Remote-research.org
breadboards: 1

parts:
  Componente2 = Arduino Mega 2560 (Rev3)
  L298N2 = L298N DC motor driver
  HC-SR04_Sensor_1 = HC-SR04 Ultrasonic Distance Sensor
  HC-SR04_Sensor_2 = HC-SR04 Ultrasonic Distance Sensor
  HC-SR04_Sensor_3 = HC-SR04 Ultrasonic Distance Sensor
  J1 = Basic Servo
  M1 = DC Motor [voltage_(max)=6V voltage_(min)=3V]
  BAT1 = 18650 Li-ion Battery [package=battery-18650]
  BAT2 = 18650 Li-ion Battery [package=battery-18650]
  BAT3 = 18650 Li-ion Battery [package=battery-18650]
  S2 = Pushbutton [package="[THT]"]
  R1 = Resistor [tolerance=±5% power=0.25 resistance=220 package=THT]
  Mod1 = Raspberry Pi 4B

nets:
  N1: Componente2.D21/SCL, Mod1.GPIO3
  N2: Componente2.D20/SDA, Mod1.GPIO2
  GND: Componente2.GND, Componente2.D37, L298N2.GND, HC-SR04_Sensor_1.GND, HC-SR04_Sensor_2.ECHO, HC-SR04_Sensor_2.GND, HC-SR04_Sensor_3.GND, BAT3.-, R1.Pin_0, Mod1.GND
  N3: Componente2.D11_PWM, L298N2.IN1
  N4: Componente2.D10_PWM, L298N2.IN2
  N5: Componente2.D8_PWM, L298N2.ENA
  3V3: Componente2.3V3, HC-SR04_Sensor_2.VCC
  VCC: Componente2.5V, HC-SR04_Sensor_1.VCC, HC-SR04_Sensor_3.VCC, S2.Pin_1, S2.Pin_2
  N6: Componente2.D3_PWM, L298N2.IN4
  N7: Componente2.D6_PWM, L298N2.IN3
  N8: Componente2.D7_PWM, J1.pulse
  N9: Componente2.D31, HC-SR04_Sensor_1.TRIG
  N10: Componente2.D40, S2.Pin_3, S2.Pin_4, R1.Pin_1
  N11: Componente2.D45, HC-SR04_Sensor_1.ECHO
  N12: Componente2.D49, HC-SR04_Sensor_2.TRIG
  N13: Componente2.D52, HC-SR04_Sensor_3.TRIG
  N14: Componente2.D53, HC-SR04_Sensor_3.ECHO
  N15: L298N2.OUT1, M1.pin_2
  N16: L298N2.OUT2, M1.pin_1
  N17: L298N2.OUT3, J1.vcc
  N18: L298N2.OUT4, J1.gnd
  N19: L298N2.12V, BAT1.+
  N20: L298N2.5V, L298N2.ENB
  N21: BAT1.-, BAT2.+
  N22: BAT2.-, BAT3.+

notes:
  We use a 10000mah power bank to energize the raspberry pi and the arduino mega.
  Also we connect a camera via USB to the raspberry pi.
  Right Sensor
  Left Sensor
  Middle Sensor

custom parts:
  L298N DC motor driver: 2x DC motor driver with 78M05 positive voltage regulator (7..35 V) L298N: max 46 V, 2 A Set 5 V Enable jumper to enable 5 V regultor (needed for the L298N) and +5 V output at screw terminal or supply external +5 V at screw terminal Set ENA and/or ENB to +5 V to enable motor permanently or supply ENA and/or ENB with PWM signal IN1 and IN2 set rotation directory for motor A (OUT1/OUT2) IN2 and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
  18650 Li-ion Battery: 18650 li-ion Battery Standard 18650 battery with interactive connectors Creative Common Attribution 4.0 International (CC-BY 4.0) license. Any use of this part requires attribution of Dr Kristofer Chan, Department of Geography, King's College London. Contact kristofer.chan [at] kcl.ac.uk OR kris [at] remote-research.org for further information.
